// Logisim project add4.circ as structural Verilog: 3 circuits, main circuit main
module main (
  input  [3:0] in_1,
  input  [3:0] in_2,
  output out_3,
  output [3:0] out_4
);

  // ADD_4 add_4_1: pin names not known; wires that end beside it: out_3, in_1, in_2, out_4, 1'b0
endmodule

module add_1 (
  input  A,
  input  B,
  input  C,
  output S,
  output V
);

  wire and_1_out, and_2_out, and_3_out, and_4_out, and_5_out, and_6_out, and_7_out, and_8_out;

  and and_1 (and_1_out, ~A, B, C);  // AND_Gate
  and and_2 (and_2_out, A, ~B, C);  // AND_Gate
  and and_3 (and_3_out, A, B, ~C);  // AND_Gate
  and and_4 (and_4_out, A, B, C);
  and and_5 (and_5_out, A, B, C);
  and and_6 (and_6_out, ~A, ~B, C);  // AND_Gate
  and and_7 (and_7_out, ~A, B, ~C);  // AND_Gate
  and and_8 (and_8_out, A, ~B, ~C);  // AND_Gate
  or or_1 (V, and_1_out, and_2_out, and_3_out, and_4_out);
  or or_2 (S, and_5_out, and_6_out, and_7_out, and_8_out);
endmodule

module ADD_4 (
  input  [3:0] in_1,
  input  [3:0] in_2,
  input  in_3,
  output out_4,
  output [3:0] out_5
);

  wire add_1_2_v, add_1_3_v, add_1_4_v;

  // Probe on in_1
  add_1 add_1_1 (.A(in_2[3]), .B(in_1[3]), .C(add_1_2_v), .S(out_5[3]), .V(out_4));
  add_1 add_1_2 (.A(in_2[2]), .B(in_1[2]), .C(add_1_3_v), .S(out_5[2]), .V(add_1_2_v));
  add_1 add_1_3 (.A(in_2[1]), .B(in_1[1]), .C(add_1_4_v), .S(out_5[1]), .V(add_1_3_v));
  // Probe on in_2
  add_1 add_1_4 (.A(in_2[0]), .B(in_1[0]), .C(in_3), .S(out_5[0]), .V(add_1_4_v));
endmodule
